# Fritzing sketch ESP32S3_AND_10K_LEVELSHIFT (saved by Fritzing 1.0.6)
circuit board: 7.2cm x 9.5cm
breadboards: 1

parts:
  TP3 = mystery part, 2 pins [chip_label=TP]
  TP2 = mystery part, 5 pins [chip_label=TP2]
  AE-LLCNV-LVCH16T245 = IC, DIP package, 48 pins [chip_label=SN74LVC16T245]
  XIXO_ESP32-S3 = IC, DIP package, 14 pins [chip_label="XIXO ESP32-S3"]
  TP4 = mystery part, 2 pins [chip_label=TP]
  TC_COM = mystery part, 4 pins [chip_label=TP_COM]
  Pi_COM = mystery part, 4 pins [chip_label=Pi_COM]
  F1 = Resettable Fuse PTC [part_number=MF-R050 package=ptc]
  TP1 = mystery part, 2 pins [chip_label=TP]
  C1 = Ceramic Capacitor [capacitance=0.1µF voltage=50V package="100 mil [THT, multilayer]"]
  C2 = Ceramic Capacitor [capacitance=0.1µF voltage=50V package="100 mil [THT, multilayer]"]
  R1-1k = Resistor [tolerance=±5% power=0.25W resistance=1k package=THT]
  R2-1k = Resistor [tolerance=±5% power=0.25W resistance=1k package=THT]
  R3_1k = Resistor [tolerance=±5% power=0.25W resistance=1k package=THT]
  R4_1k = Resistor [tolerance=±5% power=0.25W resistance=1k package=THT]
  Adruino_nano_every = Arduino Nano Every  # not connected
  TP5 = mystery part, 4 pins [chip_label=TP_COM]
  R1 = Resistor [tolerance=±5% resistance=10k package="0603 [SMD]"]
  R2 = Resistor [tolerance=±5% resistance=10k package="0603 [SMD]"]

nets:
  N1: TP3.pin1, AE-LLCNV-LVCH16T245.pin34, XIXO_ESP32-S3.pin8
  N2: TP3.pin2, AE-LLCNV-LVCH16T245.pin42, XIXO_ESP32-S3.pin7
  N3: TP2.pin1, AE-LLCNV-LVCH16T245.pin47, XIXO_ESP32-S3.pin6, R1.Pin_0
  N4: TP2.pin2, AE-LLCNV-LVCH16T245.pin46, XIXO_ESP32-S3.pin9, R2.Pin_0
  N5: TP2.pin3, AE-LLCNV-LVCH16T245.pin45, XIXO_ESP32-S3.pin5
  N6: TP2.pin4, AE-LLCNV-LVCH16T245.pin44, XIXO_ESP32-S3.pin10
  N7: TP2.pin5, AE-LLCNV-LVCH16T245.pin43, XIXO_ESP32-S3.pin13, Pi_COM.pin1, C2.0
  N8: AE-LLCNV-LVCH16T245.pin4, XIXO_ESP32-S3.pin14, F1.1, F1.2, C1.1
  N9: AE-LLCNV-LVCH16T245.pin5, TC_COM.pin1, C1.0, TP5.pin1
  N10: AE-LLCNV-LVCH16T245.pin7, TP4.pin2, R1-1k.Pin_0
  N11: AE-LLCNV-LVCH16T245.pin15, TP4.pin1, R2-1k.Pin_1
  N12: AE-LLCNV-LVCH16T245.pin48, XIXO_ESP32-S3.pin12, C2.1, R1.Pin_1, R2.Pin_1
  N13: XIXO_ESP32-S3.pin1, R3_1k.Pin_1
  N14: XIXO_ESP32-S3.pin2, R4_1k.Pin_1
  N15: TC_COM.pin3, R1-1k.Pin_1, TP5.pin3
  N16: TC_COM.pin4, R2-1k.Pin_0, TP5.pin4
  N17: Pi_COM.pin3, TP1.pin1, R4_1k.Pin_0
  N18: Pi_COM.pin4, TP1.pin2, R3_1k.Pin_0

notes:
  44 7  8  9 3v3 G 5v
  43 6  5  4  3  2  1
  G  G 28 27 26 25 25 23 22 21 18 17 16 15 14 13 12 11 G  2D 1D 2E 1E VA
  A Chanel
  G  G 28 27 26 25 25 23 22 21 18 17 16 15 14 13 12 11 G  G VB VB VA VA
  B Chanel
  GND PiRX PiTX
  44RX 43TX
  TCTX TCRX GND
  [ PIN MAP ]
  PI: G1->RX  G2<-TX
  7:OE2(L) 8:D2(L)
  PWR: VA:3.3V VB:5V
  TC: G43->RX G44<-TX
  CTRL: 5:OE1(L) 6:D1(H)
  TC UART Bridge & Level Shifter (XIAO ESP32-S3)
  G  2D 1D 2E 1E
  Ver 2026.01.13
  ESP32:G1=TX, G2=RX, G43=TX, G44=RX

custom parts:
  Arduino Nano Every: The Nano Every is Arduino’s 5V compatible board in the smallest available form factor: 45x18mm! The Arduino Nano is the preferred board for many projects requiring a small and easy to use microcontroller board. The small footprint and low price, make the Nano Every particularly suited for wearable inventions, low cost robotics, electronic musical instruments, and general use to control smaller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
