# Fritzing sketch ESP32S3_AND_LEVELSHIFT_swap (saved by Fritzing 1.0.6)
circuit board: 7.2cm x 9.5cm
breadboards: 1

parts:
  TP1 = mystery part, 2 pins [chip_label=TP]
  TP2 = mystery part, 5 pins [chip_label=TP2]
  AE-LLCNV-LVCH16T245 = IC, DIP package, 48 pins [chip_label=SN74LVC16T245]
  ESP32S3 = IC, DIP package, 14 pins [chip_label=ESP32S3]
  TP3 = mystery part, 2 pins [chip_label=TP]
  TC_COM = mystery part, 3 pins [chip_label=Pi_COM]
  TP4 = mystery part, 2 pins [chip_label=TP]
  C2 = Ceramic Capacitor [capacitance=0.1µF voltage=50V package="200 mil [THT, multilayer]"]
  C1 = Ceramic Capacitor [capacitance=0.1µF voltage=50V package="200 mil [THT, multilayer]"]
  Pi_COM = mystery part, 4 pins [chip_label=TP_COM]
  R1_1k = Resistor [tolerance=±5% power=0.25W resistance=1k package=THT]
  R2_1k = Resistor [tolerance=±5% power=0.25W resistance=1k package=THT]
  R3 = Resistor [tolerance=±5% power=0.25W resistance=1k package=THT]
  R4 = Resistor [tolerance=±5% power=0.25W resistance=1k package=THT]

nets:
  N1: TP1.pin1, AE-LLCNV-LVCH16T245.pin34, ESP32S3.pin2
  N2: TP1.pin2, AE-LLCNV-LVCH16T245.pin42, ESP32S3.pin1
  N3: TP2.pin1, AE-LLCNV-LVCH16T245.pin47, ESP32S3.pin6
  N4: TP2.pin2, AE-LLCNV-LVCH16T245.pin46, ESP32S3.pin9
  N5: TP2.pin3, AE-LLCNV-LVCH16T245.pin45, ESP32S3.pin5
  N6: TP2.pin4, AE-LLCNV-LVCH16T245.pin44, ESP32S3.pin10
  N7: TP2.pin5, AE-LLCNV-LVCH16T245.pin43, ESP32S3.pin13, C2.0, Pi_COM.pin1
  N8: AE-LLCNV-LVCH16T245.pin4, ESP32S3.pin14, C1.1
  N9: AE-LLCNV-LVCH16T245.pin5, TC_COM.pin1, C1.0
  N10: AE-LLCNV-LVCH16T245.pin7, TP4.pin2, R1_1k.Pin_1
  N11: AE-LLCNV-LVCH16T245.pin15, TP4.pin1, R2_1k.Pin_1
  N12: AE-LLCNV-LVCH16T245.pin48, ESP32S3.pin12, C2.1
  N13: ESP32S3.pin7, TP3.pin2, R3.Pin_0
  N14: ESP32S3.pin8, TP3.pin1, R4.Pin_0
  N15: TC_COM.pin2, R1_1k.Pin_0
  N16: TC_COM.pin3, R2_1k.Pin_0
  N17: Pi_COM.pin3, R4.Pin_1
  N18: Pi_COM.pin4, R3.Pin_1

notes:
  GPIO 43,44 = Pi
  Cable Swap Version
  GPIO 1,2 = TC
  43 6  5  4  3  2  1
  44 7  8  9 3v3 G 5v
  G  G 28 27 26 25 25 23 22 21 18 17 16 15 14 13 12 11 G  2D 1D 2E 1E VA
  G  G 28 27 26 25 25 23 22 21 18 17 16 15 14 13 12 11 G  G VB VB VA VA
  Ver 2026.01.09
