# Fritzing sketch FOR-TC-OC-Ver1.3.5.TC-for-Sniffer (saved by Fritzing 1.0.6)
circuit board: 9.5cm x 7.2cm
breadboards: 1

parts:
  (R1)100k = Resistor [tolerance=±5% power=0.25W resistance=100k package=THT]
  (R3)2_2k = Resistor [tolerance=±5% power=0.25W resistance=2.2k package=THT]
  D1-BAT43 = Rectifier Diode [part_number=BAT43 package="300 mil [THT]"]
  D2-BAT43 = Rectifier Diode [part_number=BAT43 package="300 mil [THT]"]
  XIXO_ESP32-S3 = IC, DIP package, 14 pins [chip_label="XIXO ESP32-S3"]
  TP4 = mystery part, 5 pins [chip_label=TC_TP]
  TP1 = mystery part, 6 pins [chip_label=Pi_COM]
  R8_1k = Resistor [tolerance=±5% power=0.25W resistance=1k package=THT]
  R9_1k = Resistor [tolerance=±5% power=0.25W resistance=1k package=THT]
  TP2 = mystery part, 2 pins [chip_label=TP]
  Pi_COM = mystery part, 6 pins [chip_label=Pi_COM]
  TP6 = mystery part, 1 pin [chip_label=TP]
  J1_2P = mystery part, 3 pins [chip_label=TP]
  (R4)100k = Resistor [tolerance=±5% power=0.25W resistance=100k package=THT]
  D4-BAT43 = Rectifier Diode [part_number=BAT43 package="300 mil [THT]"]
  D3-BAT43 = Rectifier Diode [part_number=BAT43 package="300 mil [THT]"]
  TP3 = mystery part, 5 pins [chip_label=ESP32_TP]
  TP7 = mystery part, 1 pin [chip_label=TP]
  (R2)100k = Resistor [tolerance=±5% power=0.25W resistance=100k package=THT]
  (R5)100k = Resistor [tolerance=±5% power=0.25W resistance=100k package=THT]

nets:
  N1: (R1)100k.Pin_0, TP4.pin1, J1_2P.pin3
  N2: (R1)100k.Pin_1, (R3)2_2k.Pin_0, TP6.pin1, (R2)100k.Pin_1
  N3: (R3)2_2k.Pin_1, D1-BAT43.anode, D2-BAT43.cathode, XIXO_ESP32-S3.pin4, TP3.pin1
  N4: D1-BAT43.cathode, XIXO_ESP32-S3.pin13, TP4.pin3, TP1.pin1, Pi_COM.pin1, J1_2P.pin1, D3-BAT43.cathode, TP3.pin2, (R2)100k.Pin_0, (R5)100k.Pin_0
  N5: D2-BAT43.anode, XIXO_ESP32-S3.pin12, D4-BAT43.anode, TP3.pin3
  N6: XIXO_ESP32-S3.pin1, R8_1k.Pin_1, TP2.pin2
  N7: XIXO_ESP32-S3.pin2, R9_1k.Pin_1, TP2.pin1
  N8: XIXO_ESP32-S3.pin6, D4-BAT43.cathode, TP3.pin5
  N9: XIXO_ESP32-S3.pin11, TP3.pin4
  N10: TP4.pin2, J1_2P.pin2, (R4)100k.Pin_0
  N11: TP1.pin4, R9_1k.Pin_0, Pi_COM.pin4
  N12: TP1.pin5, R8_1k.Pin_0, Pi_COM.pin5
  N13: (R4)100k.Pin_1, D3-BAT43.anode, TP7.pin1, (R5)100k.Pin_1

notes:
  SIG TX 3V GND RX
  43 6  5  4  3  2  1
  44 7  8  9 3v3 G 5v
  !24V!
  GND   SIG
  RTS RX TX 5V CTS GND
  5V-SIG
  For TC Ver1.3.5.TC only
  2026.1.30
  (TEST ONLY)
  RX TX
  TC Snifar only 2026.1.30
