# Fritzing sketch FOR-TC-OC-Ver1.3 (saved by Fritzing 1.0.6)
circuit board: 9.5cm x 7.2cm
breadboards: 1

parts:
  (R1) = Resistor [tolerance=±5% power=0.25W resistance=100k package=THT]
  (R2) = Resistor [tolerance=±5% power=0.25W resistance=15k package=THT]
  (R3) = Resistor [tolerance=±5% power=0.25W resistance=2.2k package=THT]
  D1-BAT43 = Rectifier Diode [part_number=BAT43 package="300 mil [THT]"]
  D2-BAT43 = Rectifier Diode [part_number=BAT43 package="300 mil [THT]"]
  R4_330 = Resistor [tolerance=±5% power=0.25W resistance=330 package=THT]
  R5_100k = Resistor [tolerance=±5% power=0.25W resistance=100k package=THT]
  TP3 = mystery part, 4 pins [chip_label=ESP32_TP]
  Q1-2N7000 = MOSFET-NCHANNEL [package=to220v]
  XIXO_ESP32-S3 = IC, DIP package, 14 pins [chip_label="XIXO ESP32-S3"]
  TP4 = mystery part, 5 pins [chip_label=TC_TP]
  TP1 = mystery part, 6 pins [chip_label=Pi_COM]
  R8_1k = Resistor [tolerance=±5% power=0.25W resistance=1k package=THT]
  R9_1k = Resistor [tolerance=±5% power=0.25W resistance=1k package=THT]
  TP2 = mystery part, 2 pins [chip_label=TP]
  Pi_COM = mystery part, 6 pins [chip_label=Pi_COM]
  Arduino_Nano_Every = Arduino Nano Every
  Q2-2N7001 = MOSFET-NCHANNEL [package=to220v]
  R6_4_7k = Resistor [tolerance=±5% power=0.25W resistance=4.7k package=THT]
  R7_330k = Resistor [tolerance=±5% power=0.25W resistance=330k package=THT]
  TP6 = mystery part, 1 pin [chip_label=TP]
  TP7 = mystery part, 1 pin [chip_label=TP]
  TP8 = mystery part, 1 pin [chip_label=TP]
  J1_JST_VH = rounded female pin header, 2 pins [form="♀ (female rounded)"]
  J1_JST_VH_Clean = Generic rounded female header - 2 pins [form="♀ (female rounded)" package=THT]

nets:
  N1: (R1).Pin_0, Q1-2N7000.D, TP4.pin1, J1_JST_VH.pin2
  N2: (R1).Pin_1, (R2).Pin_1, (R3).Pin_0, TP4.pin4, Arduino_Nano_Every.D10~, TP6.pin1
  N3: (R2).Pin_0, D1-BAT43.anode, R5_100k.Pin_0, TP3.pin2, Q1-2N7000.S, XIXO_ESP32-S3.pin13, TP1.pin1, Pi_COM.pin1
  N4: (R3).Pin_1, D1-BAT43.cathode, D2-BAT43.anode, TP3.pin1, XIXO_ESP32-S3.pin4
  N5: D2-BAT43.cathode, TP3.pin3, XIXO_ESP32-S3.pin12
  N6: R4_330.Pin_0, TP3.pin4, XIXO_ESP32-S3.pin11
  N7: R4_330.Pin_1, Q1-2N7000.G, TP7.pin1
  N8: R5_100k.Pin_1, TP4.pin3, Arduino_Nano_Every.GND, Arduino_Nano_Every.D13~, Q2-2N7001.S, J1_JST_VH.pin1
  N9: XIXO_ESP32-S3.pin1, R8_1k.Pin_1, TP2.pin2
  N10: XIXO_ESP32-S3.pin2, R9_1k.Pin_1, TP2.pin1
  N11: TP1.pin4, R9_1k.Pin_0, Pi_COM.pin4
  N12: TP1.pin5, R8_1k.Pin_0, Pi_COM.pin5
  N13: Arduino_Nano_Every.D11/MOSI, Arduino_Nano_Every.+5V, R6_4_7k.Pin_0, R7_330k.Pin_0
  N14: Q2-2N7001.G, R7_330k.Pin_1, TP8.pin1
  N15: Q2-2N7001.D, R6_4_7k.Pin_1
  N16: J1_JST_VH_Clean.pin1, J1_JST_VH_Clean.pin2

notes:
  TX 3V GND RX
  43 6  5  4  3  2  1
  44 7  8  9 3v3 G 5v
  !24V!
  GND   SIG
  RTS RX TX 5V CTS GND
  G  D  S
  5V-SIG
  For TC or Nano OC Connect Ver1.3.4
  2026.1.23
  (TEST ONLY)
  RX TX

custom parts:
  Arduino Nano Every: The Nano Every is Arduino’s 5V compatible board in the smallest available form factor: 45x18mm! The Arduino Nano is the preferred board for many projects requiring a small and easy to use microcontroller board. The small footprint and low price, make the Nano Every particularly suited for wearable inventions, low cost robotics, electronic musical instruments, and general use to control smaller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
  Generic rounded female header - 2 pins: Generic rounded female header
