# Fritzing sketch FOR-TC-OC-Ver1 (saved by Fritzing 1.0.6)
circuit board: 9.5cm x 7.2cm
breadboards: 1

parts:
  R1 = Resistor [tolerance=±5% power=0.25W resistance=100k package=THT]
  R2 = Resistor [tolerance=±5% power=0.25W resistance=15k package=THT]
  R3 = Resistor [tolerance=±5% power=0.25W resistance=2.2k package=THT]
  D1-BAT43 = Rectifier Diode [part_number=BAT43 package="300 mil [THT]"]
  D2-BAT43 = Rectifier Diode [part_number=BAT43 package="300 mil [THT]"]
  R4 = Resistor [tolerance=±5% power=0.25W resistance=330 package=THT]
  R5 = Resistor [tolerance=±5% power=0.25W resistance=100k package=THT]
  TP2 = mystery part, 4 pins [chip_label=ESP32_TP]
  Q1-2N7000 = MOSFET-NCHANNEL [package=to220v]
  XIXO_ESP32-S4 = IC, DIP package, 14 pins [chip_label="XIXO ESP32-S3"]
  TP1 = mystery part, 5 pins [chip_label=TC_TP]
  TP5 = mystery part, 6 pins [chip_label=Pi_COM]
  R6_1k1 = Resistor [tolerance=±5% power=0.25W resistance=1k package=THT]
  R6_1k2 = Resistor [tolerance=±5% power=0.25W resistance=1k package=THT]
  TP3 = mystery part, 2 pins [chip_label=TP]
  TP4 = mystery part, 5 pins [chip_label=TC_TP]
  Pi_COM1 = mystery part, 6 pins [chip_label=Pi_COM]

nets:
  N1: R1.Pin_0, Q1-2N7000.D, TP1.pin1, TP4.pin1
  N2: R1.Pin_1, R2.Pin_1, R3.Pin_0, TP1.pin4, TP4.pin4
  N3: R2.Pin_0, D1-BAT43.anode, R5.Pin_0, TP2.pin2, Q1-2N7000.S, XIXO_ESP32-S4.pin13, TP5.pin1, Pi_COM1.pin1
  N4: R3.Pin_1, D1-BAT43.cathode, D2-BAT43.anode, TP2.pin1, XIXO_ESP32-S4.pin4
  N5: D2-BAT43.cathode, TP2.pin3, XIXO_ESP32-S4.pin12
  N6: R4.Pin_0, TP2.pin4, XIXO_ESP32-S4.pin11
  N7: R4.Pin_1, Q1-2N7000.G
  N8: R5.Pin_1, TP1.pin3, TP4.pin3
  N9: XIXO_ESP32-S4.pin1, R6_1k1.Pin_1, TP3.pin2
  N10: XIXO_ESP32-S4.pin2, R6_1k2.Pin_1, TP3.pin1
  N11: TP5.pin4, R6_1k2.Pin_0, Pi_COM1.pin4
  N12: TP5.pin5, R6_1k1.Pin_0, Pi_COM1.pin5

notes:
  TX 3V GND RX
  43 6  5  4  3  2  1
  44 7  8  9 3v3 G 5v
  !24V!
  GND   SIG
  RTS RX TX 5V CFS GND
  G  D  S
  5VSIG
